// Logisim project CS1409_U201414800_刘一龙_cpu.circ as structural Verilog
module MIPS (
  input  [31:0] target
);

  wire ALUSham, ALUSrc, and_2_out, and_3_out, and_4_out, and_6_out, Beq, Bgtz, Bne, button_1_out,
       button_2_out, button_3_out, clk, clock_1_out, cnt1_1_value, comparator_1_eq, counter_1_q, cp0_1_ie,
       CP0RegWe, CP0ToReg, Eq, Eret, ExtOp, Halt, HasInt, Jal, Jmp, Jr, Less, LOToReg, not_1_out, not_2_out,
       not_3_out, not_4_out, or_1_out, or_2_out, RAMByte, RAMtoReg, RAMWe, RegDst, register_1_q, RegWe,
       Syscall, WriteToLO;
  wire [1:0] interruptrequest_1_intno;
  wire [2:0] cp0_1_im;
  wire [3:0] ALUOp, multiplexer_7_out_2, multiplexer_7_out_3, multiplexer_7_out_4, multiplexer_7_out_5;
  wire [4:0] multiplexer_8_out, multiplexer_9_out, multiplexer_10_out, multiplexer_11_out, rd, rs, rt, sham;
  wire [5:0] functy, op;
  wire [7:0] multiplexer_21_out;
  wire [8:0] demultiplexer_1_out0, demultiplexer_1_out1;
  wire [15:0] imm16, multiplexer_7_out;
  wire [25:0] imm26;
  wire [27:0] shifter_2_out;
  wire [31:0] a0, adder_1_out, adder_2_out, bit_extender_1_out, bit_extender_2_out, bit_extender_3_out,
       bit_extender_4_out, bit_extender_5_out, bit_extender_6_out, bit_extender_7_out, CP0RegOut,
       instruction, LO_q, main_1_reg1, multiplexer_2_out, multiplexer_3_out, multiplexer_4_out,
       multiplexer_5_out, multiplexer_6_out, multiplexer_12_out, multiplexer_13_out, multiplexer_14_out,
       multiplexer_15_out, multiplexer_16_out, multiplexer_18_out, multiplexer_19_out, multiplexer_20_out,
       OldPC, PC, R2Out, ra, ram_1_data, rom_1_data, rom_2_data, s0, s1, s2, shifter_1_out, Y;
  wire [31:1] alu_1_result;
  wire [31:28] shifter_2_out_2;

  Clock clock_1 (.out(clock_1_out));
  Counter_part #(.width(1), .max('h1), .ongoal("stay")) counter_1 (
    .load(1'b0), .count(1'b1), .Q(counter_1_q), .clk(Halt), .clr(1'b0));  // open: D, carry
  // Probe on ALUOp
  // Probe on op
  // Probe on rs
  // Probe on rt
  // Probe on rd
  // Probe on sham
  // Probe on functy
  // Probe on imm16
  // Probe on imm26
  and and_1 (clk, clock_1_out, not_1_out);
  not not_1 (not_1_out, cnt1_1_value);
  Cnt1 cnt1_1 (.enable(counter_1_q), .clk(clk), .value(cnt1_1_value));
  // Probe on s0
  Register #(.width(32)) u_PC (.D(multiplexer_6_out), .en(1'b1), .Q(PC), .clk(clk), .clr(1'b0));
  // Probe on s1
  Adder #(.width(32)) adder_1 (.a(32'h4), .b(PC), .out(adder_1_out), .cin(1'b0));  // open: cout
  Demultiplexer #(.width(9), .enable("false")) demultiplexer_1 (
    .out0(demultiplexer_1_out0), .out1(demultiplexer_1_out1), .in(PC[10:2]), .sel(PC[11]));
  IFU ifu_1 (
    .instruction(instruction), .Jmp(Jmp), .Jr(Jr), .target(main_1_reg1), .PC(PC), .Jal(Jal), .Beq(Beq),
    .Bne(Bne), .Eq(Eq), .Bgtz(Bgtz), .Eret(Eret), .OldPC(OldPC), .HasInt(HasInt), .clk(clk));  // open: R
  // Probe on s2
  not not_2 (not_2_out, Eq);
  not not_3 (not_3_out, Less);
  ROM #(.addrWidth(9), .dataWidth(32)) rom_1 (.addr(demultiplexer_1_out0), .data(rom_1_data));  // open: sel
  ROM #(.addrWidth(9), .dataWidth(32)) rom_2 (.addr(demultiplexer_1_out1), .data(rom_2_data));  // open: sel
  // Probe on ra
  and and_2 (and_2_out, Bne, not_2_out);
  and and_3 (and_3_out, Beq, Eq);
  and and_4 (and_4_out, Bgtz, not_2_out, not_3_out);
  Multiplexer #(.width(32), .enable("false")) multiplexer_1 (
    .in0(rom_1_data), .in1(rom_2_data), .out(instruction), .sel(PC[11]));
  // Probe on PC
  or or_1 (or_1_out, and_2_out, and_3_out, and_4_out);
  assign bit_extender_1_out = {{16{instruction[15]}}, instruction[15:0]};  // Bit_Extender bit_extender_1
  Shifter #(.width(32)) shifter_1 (.in(bit_extender_1_out), .\dist (5'b00010), .out(shifter_1_out));
  // Probe on instruction
  Adder #(.width(32)) adder_2 (.a(adder_1_out), .b(shifter_1_out), .out(adder_2_out), .cin(1'b0));  // open: cout
  assign bit_extender_2_out = {{6{instruction[25]}}, instruction[25:0]};  // Bit_Extender bit_extender_2
  Shifter #(.width(32)) shifter_2 (.in(bit_extender_2_out), .\dist (5'b00010), .out({shifter_2_out_2, shifter_2_out}));
  or or_2 (or_2_out, Jmp, Jal);
  Multiplexer #(.width(32), .enable("false")) multiplexer_2 (
    .in0(adder_2_out), .in1({PC[31:28], shifter_2_out}), .out(multiplexer_2_out), .sel(or_2_out));
  Multiplexer #(.width(32), .enable("false")) multiplexer_3 (
    .in0(multiplexer_2_out), .in1(target), .out(multiplexer_3_out), .sel(Jr));
  Multiplexer #(.width(32), .enable("false")) multiplexer_4 (
    .in0(adder_1_out), .in1(multiplexer_3_out), .out(multiplexer_4_out), .sel(or_1_out));
  assign bit_extender_3_out = {{20{1'b0}}, 12'h800};  // Bit_Extender bit_extender_3
  Multiplexer #(.width(32), .enable("false")) multiplexer_5 (
    .in0(multiplexer_4_out), .in1(bit_extender_3_out), .out(multiplexer_5_out), .sel(HasInt));
  Multiplexer #(.width(32), .enable("false")) multiplexer_6 (
    .in0(multiplexer_5_out), .in1(OldPC), .out(multiplexer_6_out), .sel(Eret));
  ControlUnit controlunit_1 (
    .op(op), .funct(functy), .ALUOp(ALUOp), .RegWe(RegWe), .ALUSrc(ALUSrc), .RegDst(RegDst), .ExtOp(ExtOp),
    .ALUSham(ALUSham), .RAMtoReg(RAMtoReg), .RAMWe(RAMWe), .Beq(Beq), .Bne(Bne), .Jmp(Jmp), .Jr(Jr),
    .Jal(Jal), .Syscall(Syscall), .WriteToLO(WriteToLO), .LOToReg(LOToReg), .RAMByte(RAMByte), .Bgtz(Bgtz),
    .rs(rs), .CP0RegWe(CP0RegWe), .CP0ToReg(CP0ToReg), .Eret(Eret));
  CP0 cp0_1 (
    .CP0RegOut(CP0RegOut), .CP0RegIn(Y), .clk(clk), .IntNO(interruptrequest_1_intno), .PCIn(PC),
    .IE(cp0_1_ie), .IM(cp0_1_im), .OldPC(OldPC), .rd(rd), .CP0RegWe(CP0RegWe), .HasInt(HasInt));
  Button button_1 (.out(button_1_out));
  Button button_2 (.out(button_2_out));
  Button button_3 (.out(button_3_out));
  InterruptRequest interruptrequest_1 (
    .int_1(button_1_out), .clk(clk), .int_2(button_2_out), .int_3(button_3_out), .IE(cp0_1_ie),
    .IntNO(interruptrequest_1_intno), .mask(cp0_1_im), .HasInt(HasInt));
  Pipeline_Register pipeline_register_1 ();
  Comparator #(.width(32), .mode("unsigned")) comparator_1 (
    .a(32'ha), .b(R2Out), .eq(comparator_1_eq));  // open: gt, lt
  Decoder decoder_1 (
    .instruction(instruction), .op(op), .rs(rs), .rt(rt), .rd(rd), .sham(sham), .funct(functy),
    .imm16(imm16), .imm26(imm26));
  Hex_Digit_Display hex_digit_display_1 (.value(multiplexer_7_out_5));  // open: dp
  and and_5 (Halt, comparator_1_eq, Syscall);
  Hex_Digit_Display hex_digit_display_2 (.value(multiplexer_7_out_4));  // open: dp
  Hex_Digit_Display hex_digit_display_3 (.value(multiplexer_7_out_3));  // open: dp
  and and_6 (and_6_out, not_4_out, Syscall);
  not not_4 (not_4_out, comparator_1_eq);
  Hex_Digit_Display hex_digit_display_4 (.value(multiplexer_7_out_2));  // open: dp
  Hex_Digit_Display hex_digit_display_5 (.value(multiplexer_7_out[15:12]));  // open: dp
  Multiplexer #(.width(32), .enable("false")) multiplexer_7 (
    .in0({32{1'b0}}), .in1(a0),
    .out({multiplexer_7_out_5, multiplexer_7_out_4, multiplexer_7_out_3, multiplexer_7_out_2, multiplexer_7_out}),
    .sel(register_1_q));
  Register #(.width(1)) register_1 (.D(1'b1), .en(and_6_out), .Q(register_1_q), .clk(clk));  // open: clr
  Hex_Digit_Display hex_digit_display_6 (.value(multiplexer_7_out[7:4]));  // open: dp
  Hex_Digit_Display hex_digit_display_7 (.value(multiplexer_7_out[11:8]));  // open: dp
  Hex_Digit_Display hex_digit_display_8 (.value(multiplexer_7_out[3:0]));  // open: dp
  Multiplexer #(.width(5), .enable("false")) multiplexer_8 (.in0(rt), .in1(rd), .out(multiplexer_8_out), .sel(RegDst));
  Multiplexer #(.width(5), .enable("false")) multiplexer_9 (.in0(rs), .in1(rt), .out(multiplexer_9_out), .sel(ALUSham));
  Multiplexer #(.width(5), .enable("false")) multiplexer_10 (
    .in0(rt), .in1(5'b00010), .out(multiplexer_10_out), .sel(Syscall));
  Multiplexer #(.width(5), .enable("false")) multiplexer_11 (
    .in0(multiplexer_8_out), .in1({5{1'b1}}), .out(multiplexer_11_out), .sel(Jal));
  \CS1409_U201414800_刘一龙_regfile_main  main_1 (
    .Reg1_num(multiplexer_9_out), .Reg2(multiplexer_10_out), .Write_Reg_num(multiplexer_11_out),
    .Din(multiplexer_15_out), .Write_Enable(RegWe), .Clock(clk), .Reg1(main_1_reg1), .Reg2_2(R2Out),
    .s0_Value(s0), .s1_Value(s1), .s2_Value(s2), .ra_Value(ra), .a0(a0));
  Pipeline_Register pipeline_register_2 ();
  assign bit_extender_4_out = {{16{1'b0}}, imm16};  // Bit_Extender bit_extender_4
  assign bit_extender_5_out = {{16{imm16[15]}}, imm16};  // Bit_Extender bit_extender_5
  Multiplexer #(.width(32), .enable("false")) multiplexer_12 (
    .in0(main_1_reg1), .in1(PC), .out(multiplexer_12_out), .sel(Jal));
  Multiplexer #(.width(32), .enable("false")) multiplexer_13 (
    .in0(bit_extender_4_out), .in1(bit_extender_5_out), .out(multiplexer_13_out), .sel(ExtOp));
  Multiplexer #(.width(32), .enable("false")) multiplexer_14 (
    .in0(R2Out), .in1(multiplexer_13_out), .out(multiplexer_14_out), .sel(ALUSrc));
  Register #(.width(32)) LO (.D({alu_1_result, Less}), .en(WriteToLO), .Q(LO_q), .clk(clk));  // open: clr
  Multiplexer #(.width(32), .enable("false")) multiplexer_15 (
    .in0(multiplexer_18_out), .in1(CP0RegOut), .out(multiplexer_15_out), .sel(CP0ToReg));
  assign bit_extender_6_out = {{27{1'b0}}, sham};  // Bit_Extender bit_extender_6
  Multiplexer #(.width(32), .enable("false")) multiplexer_16 (
    .in0(multiplexer_14_out), .in1(bit_extender_6_out), .out(multiplexer_16_out), .sel(ALUSham));
  Multiplexer #(.width(32), .enable("false")) multiplexer_17 (
    .in0(multiplexer_16_out), .in1(32'h4), .out(Y), .sel(Jal));
  Multiplexer #(.width(32), .enable("false")) multiplexer_18 (
    .in0(multiplexer_19_out), .in1(LO_q), .out(multiplexer_18_out), .sel(LOToReg));
  ALU alu_1 (
    .AluOP(ALUOp), .X(multiplexer_12_out), .Equal(Eq), .Result({alu_1_result, Less}), .Y(Y));  // open: Signed_Overflow, Result_2, UnSigned_Overflow
  Multiplexer #(.width(32), .enable("false")) multiplexer_19 (
    .in0({alu_1_result, Less}), .in1(multiplexer_20_out), .out(multiplexer_19_out), .sel(RAMtoReg));
  Pipeline_Register pipeline_register_3 ();
  Multiplexer #(.width(32), .enable("false")) multiplexer_20 (
    .in0(ram_1_data), .in1(bit_extender_7_out), .out(multiplexer_20_out), .sel(RAMByte));
  RAM #(.addrWidth(24), .dataWidth(32), .bus("separate")) ram_1 (
    .addr(alu_1_result[25:2]), .din(R2Out), .data(ram_1_data), .str(RAMWe), .sel(1'b1), .clk(clk), .ld(1'b1),
    .clr(1'b0));
  Multiplexer #(.select(2), .width(8), .enable("false")) multiplexer_21 (
    .in0(ram_1_data[7:0]), .in1(ram_1_data[15:8]), .in2(ram_1_data[23:16]), .in3(ram_1_data[31:24]),
    .out(multiplexer_21_out), .sel({alu_1_result[1], Less}));
  assign bit_extender_7_out = {{24{multiplexer_21_out[7]}}, multiplexer_21_out};  // Bit_Extender bit_extender_7
  Pipeline_Register pipeline_register_4 ();

  // Notes on the sheet:
  //   contents of rom_1 (hex, n*v repeats v):
  //   20110001 8000c05 20110001 20120002 20130003 8000c09 20110001 20120002 20130003 8000c0d 20110001
  //   20120002 20130003 8000c11 20110001 20120002 20130003 c000cb8 20100001 20110001 118fc0 112020
  //   20020022 c 118882 12200001 8000c15 112020 20020022 c 20110001 118880 112020 20020022 c 12200001
  //   8000c1f 20110001 118fc0 112020 20020022 c 1188c3 112020 20020022 c 118903 112020 20020022 c 118903
  //   112020 20020022 c 118903 112020 20020022 c 118903 112020 20020022 c 118903 112020 20020022 c 118903
  //   112020 20020022 c 118903 112020 20020022 c 20100001 109fc0 139fc3 8021 2012000c 24160003 26100001
  //   3210000f 20080008 20090001 139900 2709825 132020 20020022 c 1094022 1500fff9 22100001 2018000f
  //   2188024 108700 20080008 20090001 139902 2709825 132021 20020022 c 1094022 1500fff9 108702 2c9b022
  //   12c00001 8000c50 4020 1084027 84400 3508ffff 82021 20020022 c 2010ffff 20110000 ae300000 22100001
  //   22310004 ae300000 22100001 22310004 ae300000 22100001 22310004 ae300000 22100001 22310004 ae300000
  //   22100001 22310004 ae300000 22100001 22310004 ae300000 22100001 22310004 ae300000 22100001 22310004
  //   ae300000 22100001 22310004 ae300000 22100001 22310004 ae300000 22100001 22310004 ae300000 22100001
  //   22310004 ae300000 22100001 22310004 ae300000 22100001 22310004 ae300000 22100001 22310004 ae300000
  //   22100001 22310004 22100001 8020 2011003c 8e130000 8e340000 274402a 11000002 ae330000 ae140000
  //   2231fffc 1611fff8 102020 20020022 c 22100004 2011003c 1611fff2 2002000a c 20100000 22100001 102020
  //   20020022 c 22100002 102020 20020022 c 22100003 102020 20020022 c 22100004 102020 20020022 c 22100005
  //   102020 20020022 c 22100006 102020 20020022 c 22100007 102020 20020022 c 22100008 102020 20020022
  //   20020022 c 3e00008
  //   contents of rom_2 (hex, n*v repeats v):
  //   401a6000 375a0001 409a6000 201c4000 39df020 401a7000 afda0000 23de0004 23bd0004 401a6000 335afffe
  //   afda0000 23de0004 23bd0004 afd00000 23bd0004 23de0004 afd10000 23bd0004 23de0004 afd20000 23bd0004
  //   23de0004 afd30000 23bd0004 23de0004 afd40000 23bd0004 23de0004 afd50000 23bd0004 23de0004 afc40000
  //   23bd0004 23de0004 afc20000 23bd0004 23de0004 401a6800 1a9820 201b0001 175b0005 401a6000 335af9ff
  //   375a0100 409a6000 1760000c 201b0002 175b0005 401a6000 335afbff 375a0300 409a6000 17600005 201b0003
  //   175b0003 401a6000 375a0700 409a6000 401a6000 335afffe 409a6000 20020001 20120003 16530028 20110abc
  //   ac110000 20110002 80100000 20120010 102020 20020001 c 2429022 20140008 254a822 1ea00004 20140010
  //   214001b 8012 16800001 108100 1640fff3 2228822 1620ffef 20110002 80100001 20120010 102020 20020001 c
  //   2429022 20140008 254a822 1ea00004 20140010 214001b 8012 16800001 108100 1640fff3 2228822 1620ffef
  //   20120001 16400011 20110006 138020 20120010 102020 c 2429022 20140008 254a822 1ea00004 20140010
  //   214001b 8012 16800001 108100 1640fff4 2228822 1620fff0 401a6000 375a0001 409a6000 23defffc 23bdfffc
  //   8fc20000 23defffc 23bdfffc 8fc40000 23defffc 23bdfffc 8fd50000 23defffc 23bdfffc 8fd40000 23defffc
  //   23bdfffc 8fd30000 23defffc 23bdfffc 8fd20000 23defffc 23bdfffc 8fd10000 23defffc 23bdfffc 8fd00000
  //   23defffc 23bdfffc 8fda0000 409a6000 23defffc 23bdfffc 8fda0000 409a7000 401a6000 335afffe 409a6000
  //   7*0 42000018
  //   PC = PC + 4 + Offset * 4
  //   PC = PC_high_4||addr||00
  //   Syscall
  //   听说黑底绿字更好看
endmodule

module Decoder (
  input  [31:0] instruction,
  output [25:0] imm26,
  output [15:0] imm16,
  output [5:0] op,
  output [4:0] rs,
  output [4:0] rt,
  output [4:0] rd,
  output [4:0] sham,
  output [5:0] funct
);


  assign funct = instruction[5:0];
  assign imm16 = instruction[15:0];
  assign imm26 = instruction[25:0];
  assign op = instruction[31:26];
  assign rd = instruction[15:11];
  assign rs = instruction[25:21];
  assign rt = instruction[20:16];
  assign sham = instruction[10:6];

  // Notes on the sheet:
  //   R 型指令译码
  //   I 型指令译码
  //   J 型指令译码
endmodule

module InstructionTyper (
  input  [5:0] op,
  input  [5:0] functy,
  input  [4:0] rs,
  output ADD,
  output ADDI,
  output ADDIU,
  output DIVU,
  output ADDU,
  output MFLO,
  output AND,
  output LB,
  output ANDI,
  output BGTZ,
  output SLL,
  output MFC0,
  output SRA,
  output MTC0,
  output SRL,
  output ERET,
  output SUB,
  output OR,
  output ORI,
  output NOR,
  output LW,
  output SW,
  output BEQ,
  output BNE,
  output SLT,
  output SLTI,
  output SLTU,
  output JMP,
  output JAL,
  output JR,
  output SYSCALL
);

  wire not_1_out, not_2_out, not_3_out, not_4_out, not_5_out, not_6_out, not_7_out, not_8_out, not_9_out,
       not_10_out, not_11_out, not_12_out, not_13_out, not_14_out, not_15_out, not_16_out, not_17_out,
       not_18_out, not_19_out, not_20_out, not_21_out, not_22_out, not_23_out, not_24_out, not_25_out,
       not_26_out, not_27_out, not_28_out, not_29_out, not_30_out, not_31_out, not_32_out, not_33_out,
       not_34_out, not_35_out, not_36_out, not_37_out, not_38_out, not_39_out, not_40_out, not_41_out,
       not_42_out, not_43_out, not_44_out, not_45_out, not_46_out, not_47_out, not_48_out, not_49_out,
       not_50_out, not_51_out, not_52_out, not_53_out, not_54_out, not_55_out, not_56_out, not_57_out,
       not_58_out, not_59_out, not_60_out, not_61_out, not_62_out, not_63_out, not_64_out, not_65_out,
       not_66_out, not_67_out, not_68_out, not_69_out, not_70_out, not_71_out, not_72_out, not_73_out,
       not_74_out, not_75_out, not_76_out, not_77_out, not_78_out, not_79_out, not_80_out, not_81_out,
       not_82_out, not_83_out, not_84_out, not_85_out, not_86_out, not_87_out, not_88_out, not_89_out,
       not_90_out, not_91_out, not_92_out, not_93_out, not_94_out, not_95_out, not_96_out, not_97_out,
       not_98_out, not_99_out, not_100_out, not_101_out, not_102_out, not_103_out, not_104_out, not_105_out,
       not_106_out, not_107_out, not_108_out, not_109_out, not_110_out, not_111_out, not_112_out,
       not_113_out, not_114_out, not_115_out, not_116_out, not_117_out, not_118_out, not_119_out,
       not_120_out, not_121_out, not_122_out, not_123_out, not_124_out, not_125_out, not_126_out,
       not_127_out, not_128_out, not_129_out, not_130_out, not_131_out, not_132_out, not_133_out,
       not_134_out, not_135_out, not_136_out, not_137_out, not_138_out, not_139_out, not_140_out,
       not_141_out, not_142_out, not_143_out, not_144_out, not_145_out, not_146_out, not_147_out,
       not_148_out, not_149_out, not_150_out, not_151_out, not_152_out, not_153_out, not_154_out,
       not_155_out, not_156_out, not_157_out, not_158_out, not_159_out, not_160_out, not_161_out,
       not_162_out, not_163_out, not_164_out, not_165_out, not_166_out, not_167_out, not_168_out,
       not_169_out, not_170_out, not_171_out, not_172_out, not_173_out, not_174_out, not_175_out,
       not_176_out, not_177_out, not_178_out, not_179_out, not_180_out, not_181_out, not_182_out,
       not_183_out, not_184_out, not_185_out, not_186_out, not_187_out, not_188_out, not_189_out,
       not_190_out, not_191_out, not_192_out, not_193_out, not_194_out, not_195_out, not_196_out,
       not_197_out, not_198_out, not_199_out, not_200_out, not_201_out, not_202_out, not_203_out,
       not_204_out, not_205_out, not_206_out, not_207_out, not_208_out, not_209_out, not_210_out,
       not_211_out, not_212_out, not_213_out, not_214_out, not_215_out, not_216_out, not_217_out,
       not_218_out, not_219_out, not_220_out, not_221_out, not_222_out, not_223_out, not_224_out,
       not_225_out, not_226_out;

  not not_1 (not_1_out, op[5]);
  not not_2 (not_2_out, op[4]);
  not not_3 (not_3_out, op[3]);
  not not_4 (not_4_out, op[2]);
  not not_5 (not_5_out, op[1]);
  not not_6 (not_6_out, op[0]);
  not not_7 (not_7_out, functy[5]);
  not not_8 (not_8_out, functy[2]);
  not not_9 (not_9_out, op[5]);
  not not_10 (not_10_out, op[4]);
  not not_11 (not_11_out, op[3]);
  not not_12 (not_12_out, op[2]);
  not not_13 (not_13_out, op[1]);
  not not_14 (not_14_out, op[0]);
  not not_15 (not_15_out, functy[5]);
  not not_16 (not_16_out, functy[3]);
  not not_17 (not_17_out, functy[2]);
  not not_18 (not_18_out, functy[0]);
  not not_19 (not_19_out, op[4]);
  not not_20 (not_20_out, op[3]);
  not not_21 (not_21_out, op[2]);
  not not_22 (not_22_out, op[1]);
  not not_23 (not_23_out, op[0]);
  not not_24 (not_24_out, op[5]);
  not not_25 (not_25_out, op[4]);
  not not_26 (not_26_out, op[3]);
  not not_27 (not_27_out, op[5]);
  not not_28 (not_28_out, op[3]);
  not not_29 (not_29_out, op[2]);
  not not_30 (not_30_out, op[1]);
  not not_31 (not_31_out, op[0]);
  not not_32 (not_32_out, rs[4]);
  not not_33 (not_33_out, rs[3]);
  not not_34 (not_34_out, rs[2]);
  not not_35 (not_35_out, rs[1]);
  not not_36 (not_36_out, rs[0]);
  not not_37 (not_37_out, op[5]);
  not not_38 (not_38_out, op[3]);
  not not_39 (not_39_out, op[2]);
  not not_40 (not_40_out, op[1]);
  not not_41 (not_41_out, op[0]);
  not not_42 (not_42_out, rs[4]);
  not not_43 (not_43_out, rs[3]);
  not not_44 (not_44_out, rs[1]);
  not not_45 (not_45_out, rs[0]);
  not not_46 (not_46_out, op[5]);
  not not_47 (not_47_out, op[3]);
  not not_48 (not_48_out, op[2]);
  not not_49 (not_49_out, op[1]);
  not not_50 (not_50_out, op[0]);
  not not_51 (not_51_out, functy[5]);
  not not_52 (not_52_out, functy[2]);
  not not_53 (not_53_out, functy[1]);
  not not_54 (not_54_out, functy[0]);
  and and_1 (LB, op[5], not_19_out, not_20_out, not_21_out, not_22_out, not_23_out);
  and and_2 (BGTZ, not_24_out, not_25_out, not_26_out, op[2], op[1], op[0]);
  and and_3 (MFC0, not_27_out, op[4], not_28_out, not_29_out, not_30_out, not_31_out, not_32_out, not_33_out, not_34_out, not_35_out, not_36_out);
  and and_4 (MTC0, not_37_out, op[4], not_38_out, not_39_out, not_40_out, not_41_out, not_42_out, not_43_out, rs[2], not_44_out, not_45_out);
  and and_5 (ERET, not_46_out, op[4], not_47_out, not_48_out, not_49_out, not_50_out, not_51_out, functy[4], functy[3], not_52_out, not_53_out, not_54_out);
  and and_6 (DIVU, not_1_out, not_2_out, not_3_out, not_4_out, not_5_out, not_6_out, not_7_out, functy[4], functy[3], not_8_out, functy[1], functy[0]);
  and and_7 (MFLO, not_9_out, not_10_out, not_11_out, not_12_out, not_13_out, not_14_out, not_15_out, functy[4], not_16_out, not_17_out, functy[1], not_18_out);
  not not_55 (not_55_out, op[5]);
  not not_56 (not_56_out, op[4]);
  not not_57 (not_57_out, op[3]);
  not not_58 (not_58_out, op[2]);
  not not_59 (not_59_out, op[1]);
  not not_60 (not_60_out, op[0]);
  not not_61 (not_61_out, functy[4]);
  not not_62 (not_62_out, functy[3]);
  not not_63 (not_63_out, functy[2]);
  not not_64 (not_64_out, functy[1]);
  not not_65 (not_65_out, functy[0]);
  not not_66 (not_66_out, op[5]);
  not not_67 (not_67_out, op[4]);
  not not_68 (not_68_out, op[2]);
  not not_69 (not_69_out, op[1]);
  not not_70 (not_70_out, op[0]);
  not not_71 (not_71_out, op[5]);
  not not_72 (not_72_out, op[4]);
  not not_73 (not_73_out, op[2]);
  not not_74 (not_74_out, op[1]);
  not not_75 (not_75_out, op[5]);
  not not_76 (not_76_out, op[4]);
  not not_77 (not_77_out, op[3]);
  not not_78 (not_78_out, op[2]);
  not not_79 (not_79_out, op[1]);
  not not_80 (not_80_out, op[0]);
  not not_81 (not_81_out, functy[4]);
  not not_82 (not_82_out, functy[3]);
  not not_83 (not_83_out, functy[2]);
  not not_84 (not_84_out, functy[1]);
  not not_85 (not_85_out, op[5]);
  not not_86 (not_86_out, op[4]);
  not not_87 (not_87_out, op[3]);
  not not_88 (not_88_out, op[2]);
  not not_89 (not_89_out, op[1]);
  not not_90 (not_90_out, op[0]);
  not not_91 (not_91_out, functy[4]);
  not not_92 (not_92_out, functy[3]);
  not not_93 (not_93_out, functy[1]);
  not not_94 (not_94_out, functy[0]);
  not not_95 (not_95_out, op[5]);
  not not_96 (not_96_out, op[4]);
  not not_97 (not_97_out, op[1]);
  not not_98 (not_98_out, op[0]);
  not not_99 (not_99_out, op[5]);
  not not_100 (not_100_out, op[4]);
  not not_101 (not_101_out, op[3]);
  not not_102 (not_102_out, op[2]);
  not not_103 (not_103_out, op[1]);
  not not_104 (not_104_out, op[0]);
  not not_105 (not_105_out, functy[5]);
  not not_106 (not_106_out, functy[4]);
  not not_107 (not_107_out, functy[3]);
  not not_108 (not_108_out, functy[2]);
  not not_109 (not_109_out, functy[1]);
  not not_110 (not_110_out, functy[0]);
  not not_111 (not_111_out, op[5]);
  not not_112 (not_112_out, op[4]);
  not not_113 (not_113_out, op[3]);
  not not_114 (not_114_out, op[2]);
  not not_115 (not_115_out, op[1]);
  not not_116 (not_116_out, op[0]);
  not not_117 (not_117_out, functy[5]);
  not not_118 (not_118_out, functy[4]);
  not not_119 (not_119_out, functy[3]);
  not not_120 (not_120_out, functy[2]);
  not not_121 (not_121_out, op[5]);
  not not_122 (not_122_out, op[4]);
  not not_123 (not_123_out, op[3]);
  not not_124 (not_124_out, op[2]);
  not not_125 (not_125_out, op[1]);
  not not_126 (not_126_out, op[0]);
  not not_127 (not_127_out, functy[5]);
  not not_128 (not_128_out, functy[4]);
  not not_129 (not_129_out, functy[3]);
  not not_130 (not_130_out, functy[2]);
  not not_131 (not_131_out, functy[0]);
  not not_132 (not_132_out, op[5]);
  not not_133 (not_133_out, op[4]);
  not not_134 (not_134_out, op[3]);
  not not_135 (not_135_out, op[2]);
  not not_136 (not_136_out, op[1]);
  not not_137 (not_137_out, op[0]);
  not not_138 (not_138_out, functy[4]);
  not not_139 (not_139_out, functy[3]);
  not not_140 (not_140_out, functy[2]);
  not not_141 (not_141_out, functy[0]);
  not not_142 (not_142_out, op[5]);
  not not_143 (not_143_out, op[4]);
  not not_144 (not_144_out, op[3]);
  not not_145 (not_145_out, op[2]);
  not not_146 (not_146_out, op[1]);
  not not_147 (not_147_out, op[0]);
  not not_148 (not_148_out, functy[4]);
  not not_149 (not_149_out, functy[3]);
  not not_150 (not_150_out, functy[1]);
  not not_151 (not_151_out, op[5]);
  not not_152 (not_152_out, op[4]);
  not not_153 (not_153_out, op[1]);
  not not_154 (not_154_out, op[5]);
  not not_155 (not_155_out, op[4]);
  not not_156 (not_156_out, op[3]);
  not not_157 (not_157_out, op[2]);
  not not_158 (not_158_out, op[1]);
  not not_159 (not_159_out, op[0]);
  not not_160 (not_160_out, functy[4]);
  not not_161 (not_161_out, functy[3]);
  not not_162 (not_162_out, op[4]);
  not not_163 (not_163_out, op[3]);
  not not_164 (not_164_out, op[2]);
  not not_165 (not_165_out, op[4]);
  not not_166 (not_166_out, op[2]);
  not not_167 (not_167_out, op[5]);
  not not_168 (not_168_out, op[4]);
  not not_169 (not_169_out, op[3]);
  not not_170 (not_170_out, op[1]);
  not not_171 (not_171_out, op[0]);
  not not_172 (not_172_out, op[5]);
  not not_173 (not_173_out, op[4]);
  not not_174 (not_174_out, op[3]);
  not not_175 (not_175_out, op[1]);
  not not_176 (not_176_out, op[5]);
  not not_177 (not_177_out, op[4]);
  not not_178 (not_178_out, op[3]);
  not not_179 (not_179_out, op[2]);
  not not_180 (not_180_out, op[1]);
  not not_181 (not_181_out, op[0]);
  not not_182 (not_182_out, functy[4]);
  not not_183 (not_183_out, functy[2]);
  not not_184 (not_184_out, functy[0]);
  not not_185 (not_185_out, op[5]);
  not not_186 (not_186_out, op[4]);
  not not_187 (not_187_out, op[2]);
  not not_188 (not_188_out, op[0]);
  not not_189 (not_189_out, op[5]);
  not not_190 (not_190_out, op[4]);
  not not_191 (not_191_out, op[3]);
  not not_192 (not_192_out, op[2]);
  not not_193 (not_193_out, op[1]);
  not not_194 (not_194_out, op[0]);
  not not_195 (not_195_out, functy[4]);
  not not_196 (not_196_out, functy[2]);
  not not_197 (not_197_out, op[5]);
  not not_198 (not_198_out, op[4]);
  not not_199 (not_199_out, op[3]);
  not not_200 (not_200_out, op[2]);
  not not_201 (not_201_out, op[0]);
  not not_202 (not_202_out, op[5]);
  not not_203 (not_203_out, op[4]);
  not not_204 (not_204_out, op[3]);
  not not_205 (not_205_out, op[2]);
  not not_206 (not_206_out, op[5]);
  not not_207 (not_207_out, op[4]);
  not not_208 (not_208_out, op[3]);
  not not_209 (not_209_out, op[2]);
  not not_210 (not_210_out, op[1]);
  not not_211 (not_211_out, op[0]);
  not not_212 (not_212_out, functy[5]);
  not not_213 (not_213_out, functy[4]);
  not not_214 (not_214_out, functy[2]);
  not not_215 (not_215_out, functy[1]);
  not not_216 (not_216_out, functy[0]);
  not not_217 (not_217_out, op[5]);
  not not_218 (not_218_out, op[4]);
  not not_219 (not_219_out, op[3]);
  not not_220 (not_220_out, op[2]);
  not not_221 (not_221_out, op[1]);
  not not_222 (not_222_out, op[0]);
  not not_223 (not_223_out, functy[5]);
  not not_224 (not_224_out, functy[4]);
  not not_225 (not_225_out, functy[1]);
  not not_226 (not_226_out, functy[0]);
  and and_8 (ADD, not_55_out, not_56_out, not_57_out, not_58_out, not_59_out, not_60_out, functy[5], not_61_out, not_62_out, not_63_out, not_64_out, not_65_out);
  and and_9 (ADDI, not_66_out, not_67_out, op[3], not_68_out, not_69_out, not_70_out);
  and and_10 (ADDIU, not_71_out, not_72_out, op[3], not_73_out, not_74_out, op[0]);
  and and_11 (ADDU, not_75_out, not_76_out, not_77_out, not_78_out, not_79_out, not_80_out, functy[5], not_81_out, not_82_out, not_83_out, not_84_out, functy[0]);
  and and_12 (AND, not_85_out, not_86_out, not_87_out, not_88_out, not_89_out, not_90_out, functy[5], not_91_out, not_92_out, functy[2], not_93_out, not_94_out);
  and and_13 (ANDI, not_95_out, not_96_out, op[3], op[2], not_97_out, not_98_out);
  and and_14 (SLL, not_99_out, not_100_out, not_101_out, not_102_out, not_103_out, not_104_out, not_105_out, not_106_out, not_107_out, not_108_out, not_109_out, not_110_out);
  and and_15 (SRA, not_111_out, not_112_out, not_113_out, not_114_out, not_115_out, not_116_out, not_117_out, not_118_out, not_119_out, not_120_out, functy[1], functy[0]);
  and and_16 (SRL, not_121_out, not_122_out, not_123_out, not_124_out, not_125_out, not_126_out, not_127_out, not_128_out, not_129_out, not_130_out, functy[1], not_131_out);
  and and_17 (SUB, not_132_out, not_133_out, not_134_out, not_135_out, not_136_out, not_137_out, functy[5], not_138_out, not_139_out, not_140_out, functy[1], not_141_out);
  and and_18 (OR, not_142_out, not_143_out, not_144_out, not_145_out, not_146_out, not_147_out, functy[5], not_148_out, not_149_out, functy[2], not_150_out, functy[0]);
  and and_19 (ORI, not_151_out, not_152_out, op[3], op[2], not_153_out, op[0]);
  and and_20 (NOR, not_154_out, not_155_out, not_156_out, not_157_out, not_158_out, not_159_out, functy[5], not_160_out, not_161_out, functy[2], functy[1], functy[0]);
  and and_21 (LW, op[5], not_162_out, not_163_out, not_164_out, op[1], op[0]);
  and and_22 (SW, op[5], not_165_out, op[3], not_166_out, op[1], op[0]);
  and and_23 (BEQ, not_167_out, not_168_out, not_169_out, op[2], not_170_out, not_171_out);
  and and_24 (BNE, not_172_out, not_173_out, not_174_out, op[2], not_175_out, op[0]);
  and and_25 (SLT, not_176_out, not_177_out, not_178_out, not_179_out, not_180_out, not_181_out, functy[5], not_182_out, functy[3], not_183_out, functy[1], not_184_out);
  and and_26 (SLTI, not_185_out, not_186_out, op[3], not_187_out, op[1], not_188_out);
  and and_27 (SLTU, not_189_out, not_190_out, not_191_out, not_192_out, not_193_out, not_194_out, functy[5], not_195_out, functy[3], not_196_out, functy[1], functy[0]);
  and and_28 (JMP, not_197_out, not_198_out, not_199_out, not_200_out, op[1], not_201_out);
  and and_29 (JAL, not_202_out, not_203_out, not_204_out, not_205_out, op[1], op[0]);
  and and_30 (JR, not_206_out, not_207_out, not_208_out, not_209_out, not_210_out, not_211_out, not_212_out, not_213_out, functy[3], not_214_out, not_215_out, not_216_out);
  and and_31 (SYSCALL, not_217_out, not_218_out, not_219_out, not_220_out, not_221_out, not_222_out, not_223_out, not_224_out, functy[3], functy[2], not_225_out, not_226_out);

  // Other names for the same wires on the sheet: FU0 = functy[0]; FU1 = functy[1]; FU2 = functy[2]; FU3 = functy[3];
  //   FU4 = functy[4]; FU5 = functy[5]
endmodule

module IFU (
  input  [31:0] target,
  input  [31:0] OldPC,
  input  Beq,
  input  Jr,
  input  HasInt,
  input  Eret,
  input  Bne,
  input  Eq,
  input  Jmp,
  input  Jal,
  input  Bgtz,
  input  R,
  input  clk,
  output [31:0] instruction,
  output [31:0] PC
);

  wire and_1_out, and_2_out, and_3_out, not_1_out, not_2_out, or_1_out, or_2_out;
  wire [8:0] demultiplexer_1_out0, demultiplexer_1_out1;
  wire [27:0] shifter_2_out;
  wire [31:0] adder_1_out, adder_2_out, bit_extender_1_out, bit_extender_2_out, bit_extender_3_out,
       multiplexer_2_out, multiplexer_3_out, multiplexer_4_out, multiplexer_5_out, multiplexer_6_out,
       rom_1_data, rom_2_data, shifter_1_out;
  wire [31:28] shifter_2_out_2;

  Demultiplexer #(.width(9), .enable("false")) demultiplexer_1 (
    .out0(demultiplexer_1_out0), .out1(demultiplexer_1_out1), .in(PC[10:2]), .sel(PC[11]));
  Register #(.width(32)) u_PC (.D(multiplexer_6_out), .en(1'b1), .Q(PC), .clk(clk), .clr(1'b0));
  Adder #(.width(32)) adder_1 (.a(32'h4), .b(PC), .out(adder_1_out), .cin(1'b0));  // open: cout
  and and_1 (and_1_out, Bne, not_1_out);
  not not_1 (not_1_out, Eq);
  and and_2 (and_2_out, Beq, Eq);
  and and_3 (and_3_out, Bgtz, not_1_out, not_2_out);
  not not_2 (not_2_out, R);
  ROM #(.addrWidth(9), .dataWidth(32)) rom_1 (.addr(demultiplexer_1_out0), .data(rom_1_data));  // open: sel
  Multiplexer #(.width(32), .enable("false")) multiplexer_1 (
    .in0(rom_1_data), .in1(rom_2_data), .out(instruction), .sel(PC[11]));
  ROM #(.addrWidth(9), .dataWidth(32)) rom_2 (.addr(demultiplexer_1_out1), .data(rom_2_data));  // open: sel
  or or_1 (or_1_out, and_1_out, and_2_out, and_3_out);
  assign bit_extender_1_out = {{16{instruction[15]}}, instruction[15:0]};  // Bit_Extender bit_extender_1
  Adder #(.width(32)) adder_2 (.a(adder_1_out), .b(shifter_1_out), .out(adder_2_out), .cin(1'b0));  // open: cout
  Shifter #(.width(32)) shifter_1 (.in(bit_extender_1_out), .\dist (5'b00010), .out(shifter_1_out));
  assign bit_extender_2_out = {{6{instruction[25]}}, instruction[25:0]};  // Bit_Extender bit_extender_2
  Shifter #(.width(32)) shifter_2 (.in(bit_extender_2_out), .\dist (5'b00010), .out({shifter_2_out_2, shifter_2_out}));
  Multiplexer #(.width(32), .enable("false")) multiplexer_2 (
    .in0(adder_2_out), .in1({PC[31:28], shifter_2_out}), .out(multiplexer_2_out), .sel(or_2_out));
  or or_2 (or_2_out, Jmp, Jal);
  Multiplexer #(.width(32), .enable("false")) multiplexer_3 (
    .in0(multiplexer_2_out), .in1(target), .out(multiplexer_3_out), .sel(Jr));
  Multiplexer #(.width(32), .enable("false")) multiplexer_4 (
    .in0(adder_1_out), .in1(multiplexer_3_out), .out(multiplexer_4_out), .sel(or_1_out));
  assign bit_extender_3_out = {{20{1'b0}}, 12'h800};  // Bit_Extender bit_extender_3
  Multiplexer #(.width(32), .enable("false")) multiplexer_5 (
    .in0(multiplexer_4_out), .in1(bit_extender_3_out), .out(multiplexer_5_out), .sel(HasInt));
  Multiplexer #(.width(32), .enable("false")) multiplexer_6 (
    .in0(multiplexer_5_out), .in1(OldPC), .out(multiplexer_6_out), .sel(Eret));

  // Notes on the sheet:
  //   contents of rom_1 (hex, n*v repeats v):
  //   20110001 8000c05 20110001 20120002 20130003 8000c09 20110001 20120002 20130003 8000c0d 20110001
  //   20120002 20130003 8000c11 20110001 20120002 20130003 c000cb8 20100001 20110001 118fc0 112020
  //   20020022 c 118882 12200001 8000c15 112020 20020022 c 20110001 118880 112020 20020022 c 12200001
  //   8000c1f 20110001 118fc0 112020 20020022 c 1188c3 112020 20020022 c 118903 112020 20020022 c 118903
  //   112020 20020022 c 118903 112020 20020022 c 118903 112020 20020022 c 118903 112020 20020022 c 118903
  //   112020 20020022 c 118903 112020 20020022 c 20100001 109fc0 139fc3 8021 2012000c 24160003 26100001
  //   3210000f 20080008 20090001 139900 2709825 132020 20020022 c 1094022 1500fff9 22100001 2018000f
  //   2188024 108700 20080008 20090001 139902 2709825 132021 20020022 c 1094022 1500fff9 108702 2c9b022
  //   12c00001 8000c50 4020 1084027 84400 3508ffff 82021 20020022 c 2010ffff 20110000 ae300000 22100001
  //   22310004 ae300000 22100001 22310004 ae300000 22100001 22310004 ae300000 22100001 22310004 ae300000
  //   22100001 22310004 ae300000 22100001 22310004 ae300000 22100001 22310004 ae300000 22100001 22310004
  //   ae300000 22100001 22310004 ae300000 22100001 22310004 ae300000 22100001 22310004 ae300000 22100001
  //   22310004 ae300000 22100001 22310004 ae300000 22100001 22310004 ae300000 22100001 22310004 ae300000
  //   22100001 22310004 22100001 8020 2011003c 8e130000 8e340000 274402a 11000002 ae330000 ae140000
  //   2231fffc 1611fff8 102020 20020022 c 22100004 2011003c 1611fff2 2002000a c 20100000 22100001 102020
  //   20020022 c 22100002 102020 20020022 c 22100003 102020 20020022 c 22100004 102020 20020022 c 22100005
  //   102020 20020022 c 22100006 102020 20020022 c 22100007 102020 20020022 c 22100008 102020 20020022
  //   20020022 c 3e00008
  //   contents of rom_2 (hex, n*v repeats v):
  //   401a6000 375a0001 409a6000 201c4000 39df020 401a7000 afda0000 23de0004 23bd0004 401a6000 335afffe
  //   afda0000 23de0004 23bd0004 afd00000 23bd0004 23de0004 afd10000 23bd0004 23de0004 afd20000 23bd0004
  //   23de0004 afd30000 23bd0004 23de0004 afd40000 23bd0004 23de0004 afd50000 23bd0004 23de0004 afc40000
  //   23bd0004 23de0004 afc20000 23bd0004 23de0004 401a6800 1a9820 201b0001 175b0005 401a6000 335af9ff
  //   375a0100 409a6000 1760000c 201b0002 175b0005 401a6000 335afbff 375a0300 409a6000 17600005 201b0003
  //   175b0003 401a6000 375a0700 409a6000 401a6000 335afffe 409a6000 20020001 20120003 16530028 20110abc
  //   ac110000 20110002 80100000 20120010 102020 20020001 c 2429022 20140008 254a822 1ea00004 20140010
  //   214001b 8012 16800001 108100 1640fff3 2228822 1620ffef 20110002 80100001 20120010 102020 20020001 c
  //   2429022 20140008 254a822 1ea00004 20140010 214001b 8012 16800001 108100 1640fff3 2228822 1620ffef
  //   20120001 16400011 20110006 138020 20120010 102020 c 2429022 20140008 254a822 1ea00004 20140010
  //   214001b 8012 16800001 108100 1640fff4 2228822 1620fff0 401a6000 375a0001 409a6000 23defffc 23bdfffc
  //   8fc20000 23defffc 23bdfffc 8fc40000 23defffc 23bdfffc 8fd50000 23defffc 23bdfffc 8fd40000 23defffc
  //   23bdfffc 8fd30000 23defffc 23bdfffc 8fd20000 23defffc 23bdfffc 8fd10000 23defffc 23bdfffc 8fd00000
  //   23defffc 23bdfffc 8fda0000 409a6000 23defffc 23bdfffc 8fda0000 409a7000 401a6000 335afffe 409a6000
  //   7*0 42000018
  //   PC = PC + 4 + Offset * 4
  //   PC = PC_high_4||addr||00
endmodule

module ControlUnit (
  input  [5:0] op,
  input  [5:0] funct,
  input  [4:0] rs,
  output [3:0] ALUOp,
  output ALUSrc,
  output RegDst,
  output ExtOp,
  output ALUSham,
  output RAMtoReg,
  output RAMWe,
  output Beq,
  output Bne,
  output Jmp,
  output Jal,
  output Jr,
  output Syscall,
  output WriteToLO,
  output LOToReg,
  output RAMByte,
  output Bgtz,
  output CP0ToReg,
  output CP0RegWe,
  output Eret,
  output RegWe
);

  wire instructiontyper_1_add, instructiontyper_1_addi, instructiontyper_1_addiu, instructiontyper_1_addu,
       instructiontyper_1_and, instructiontyper_1_andi, instructiontyper_1_beq, instructiontyper_1_bne,
       instructiontyper_1_lw, instructiontyper_1_nor, instructiontyper_1_or, instructiontyper_1_ori,
       instructiontyper_1_sll, instructiontyper_1_slt, instructiontyper_1_slti, instructiontyper_1_sltu,
       instructiontyper_1_sra, instructiontyper_1_srl, instructiontyper_1_sub;

  InstructionTyper instructiontyper_1 (
    .op(op), .functy(funct), .ADD(instructiontyper_1_add), .ADDI(instructiontyper_1_addi),
    .ADDIU(instructiontyper_1_addiu), .ADDU(instructiontyper_1_addu), .AND(instructiontyper_1_and),
    .ANDI(instructiontyper_1_andi), .SLL(instructiontyper_1_sll), .SRA(instructiontyper_1_sra),
    .SRL(instructiontyper_1_srl), .SUB(instructiontyper_1_sub), .OR(instructiontyper_1_or),
    .ORI(instructiontyper_1_ori), .NOR(instructiontyper_1_nor), .LW(instructiontyper_1_lw), .SW(RAMWe),
    .BEQ(instructiontyper_1_beq), .BNE(instructiontyper_1_bne), .SLT(instructiontyper_1_slt),
    .SLTI(instructiontyper_1_slti), .SLTU(instructiontyper_1_sltu), .JMP(Jmp), .JAL(Jal), .JR(Jr),
    .SYSCALL(Syscall), .DIVU(WriteToLO), .MFLO(LOToReg), .LB(RAMByte), .BGTZ(Bgtz), .rs(rs), .MFC0(CP0ToReg),
    .MTC0(CP0RegWe), .ERET(Eret));
  or or_1 (ALUOp[0], instructiontyper_1_add, instructiontyper_1_addi, instructiontyper_1_addiu, instructiontyper_1_addu, instructiontyper_1_and, instructiontyper_1_andi, instructiontyper_1_sra, instructiontyper_1_lw, RAMWe, instructiontyper_1_slt, instructiontyper_1_slti, Jal, RAMByte, Bgtz);
  or or_2 (ALUOp[1], instructiontyper_1_and, instructiontyper_1_andi, instructiontyper_1_srl, instructiontyper_1_sub, instructiontyper_1_nor, instructiontyper_1_slt, instructiontyper_1_slti, Bgtz);
  or or_3 (ALUOp[2], instructiontyper_1_add, instructiontyper_1_addi, instructiontyper_1_addiu, instructiontyper_1_addu, instructiontyper_1_and, instructiontyper_1_andi, instructiontyper_1_sub, instructiontyper_1_lw, RAMWe, instructiontyper_1_sltu, Jal, WriteToLO, RAMByte);
  or or_4 (ALUOp[3], instructiontyper_1_or, instructiontyper_1_ori, instructiontyper_1_nor, instructiontyper_1_slt, instructiontyper_1_slti, instructiontyper_1_sltu, Bgtz);
  or or_5 (RegWe, instructiontyper_1_add, instructiontyper_1_addi, instructiontyper_1_addiu, instructiontyper_1_addu, instructiontyper_1_and, instructiontyper_1_andi, instructiontyper_1_sll, instructiontyper_1_sra, instructiontyper_1_srl, instructiontyper_1_sub, instructiontyper_1_or, instructiontyper_1_ori, instructiontyper_1_nor, instructiontyper_1_lw, instructiontyper_1_slt, instructiontyper_1_slti, instructiontyper_1_sltu, Jal, LOToReg, RAMByte, CP0ToReg);
  or or_6 (ALUSrc, instructiontyper_1_addi, instructiontyper_1_addiu, instructiontyper_1_andi, instructiontyper_1_ori, instructiontyper_1_lw, RAMWe, instructiontyper_1_slti, RAMByte);
  or or_7 (RegDst, instructiontyper_1_add, instructiontyper_1_addu, instructiontyper_1_and, instructiontyper_1_sll, instructiontyper_1_sra, instructiontyper_1_srl, instructiontyper_1_sub, instructiontyper_1_or, instructiontyper_1_nor, instructiontyper_1_slt, instructiontyper_1_sltu, LOToReg);
  or or_8 (ExtOp, instructiontyper_1_addi, instructiontyper_1_addiu, instructiontyper_1_lw, RAMWe, instructiontyper_1_slti, RAMByte);
  or or_9 (ALUSham, instructiontyper_1_sll, instructiontyper_1_sra, instructiontyper_1_srl);
  or or_10 (RAMtoReg, instructiontyper_1_lw, RAMByte);
  or or_11 (Beq, instructiontyper_1_beq, Jmp, Jal, Jr);
  or or_12 (Bne, instructiontyper_1_bne, Jmp, Jal, Jr);
endmodule

module InterruptRequest (
  input  int_1,
  input  int_2,
  input  IE,
  input  int_3,
  input  [2:0] mask,
  input  clk,
  output [1:0] IntNO,
  output HasInt
);

  wire and_1_out, and_2_out, and_3_out, clear_1, clear_2, clear_3, comparator_1_eq, mask_1_q, mask_2_q,
       mask_3_q, multiplexer_1_out, not_1_out, not_2_out, priority_encoder_1_en_out, priority_encoder_1_gs,
       register_1_q, register_2_q, register_3_q, register_4_q;
  wire [1:0] counter_1_q, priority_encoder_1_out;

  Register #(.width(1)) register_1 (.D(1'b1), .Q(register_1_q), .clk(int_1), .clr(clear_1));  // open: en
  Register #(.width(1)) register_2 (.D(1'b1), .Q(register_2_q), .clk(int_2), .clr(clear_2));  // open: en
  Register #(.width(1)) register_3 (.D(1'b1), .Q(register_3_q), .clk(int_3), .clr(clear_3));  // open: en
  Register #(.width(1)) mask_1 (.D(mask[0]), .Q(mask_1_q), .clk(clk));  // open: en, clr
  Register #(.width(1)) mask_2 (.D(mask[1]), .Q(mask_2_q), .clk(clk));  // open: en, clr
  Register #(.width(1)) mask_3 (.D(mask[2]), .Q(mask_3_q), .clk(clk));  // open: en, clr
  and and_1 (and_1_out, register_1_q, ~mask_1_q);  // AND_Gate
  and and_2 (and_2_out, register_2_q, ~mask_2_q);  // AND_Gate
  and and_3 (and_3_out, register_3_q, ~mask_3_q);  // AND_Gate
  Multiplexer #(.select(2), .enable("false")) multiplexer_1 (
    .in0(1'b0), .in1(register_1_q), .in2(register_2_q), .in3(register_3_q), .out(multiplexer_1_out),
    .sel(IntNO));
  Counter_part #(.width(2), .max('h3)) counter_1 (
    .Q(counter_1_q), .clk(not_1_out));  // open: load, D, count, carry, clr
  not not_1 (not_1_out, clk);
  Priority_Encoder #(.select(2)) priority_encoder_1 (
    .in1(and_1_out), .in2(and_2_out), .in3(and_3_out), .out(priority_encoder_1_out),
    .gs(priority_encoder_1_gs), .en_out(priority_encoder_1_en_out));  // open: in0, en_in
  Comparator #(.width(2)) comparator_1 (.a(2'b11), .b(counter_1_q), .eq(comparator_1_eq));  // open: gt, lt
  Multiplexer #(.width(2), .enable("false")) multiplexer_2 (
    .in0(priority_encoder_1_out), .in1(2'b00), .out(IntNO), .sel(priority_encoder_1_en_out));
  and and_4 (HasInt, priority_encoder_1_gs, comparator_1_eq, IE);
  not not_2 (not_2_out, multiplexer_1_out);
  Demultiplexer #(.select(2), .enable("false")) demultiplexer_1 (
    .out1(clear_1), .out2(clear_2), .out3(clear_3), .in(register_4_q), .sel(IntNO));  // open: out0
  Register #(.width(1), .trigger("falling")) register_4 (
    .D(1'b1), .Q(register_4_q), .clk(HasInt), .clr(not_2_out));  // open: en
endmodule

module CP0 (
  input  clk,
  input  [31:0] CP0RegIn,
  input  [1:0] IntNO,
  input  [31:0] PCIn,
  input  HasInt,
  input  [4:0] rd,
  input  CP0RegWe,
  output [2:0] IM,
  output IE,
  output [31:0] CP0RegOut,
  output [31:0] OldPC
);

  wire demultiplexer_1_out12, demultiplexer_1_out14, or_1_out;
  wire [31:0] bit_extender_1_out, Cause_q, multiplexer_1_out, OldPC_q, Status_q;

  Register #(.width(32)) u_OldPC (.D(PCIn), .Q(OldPC_q), .clk(HasInt));  // open: en, clr
  assign bit_extender_1_out = {{30{1'b0}}, IntNO};  // Bit_Extender bit_extender_1
  Multiplexer #(.width(32), .enable("false")) multiplexer_1 (
    .in0(CP0RegIn), .in1(OldPC_q), .out(multiplexer_1_out), .sel(HasInt));
  or or_1 (or_1_out, demultiplexer_1_out14, HasInt);
  Demultiplexer #(.select(5), .enable("false")) demultiplexer_1 (
    .out12(demultiplexer_1_out12), .out14(demultiplexer_1_out14), .in(CP0RegWe), .sel(rd));  // open: out0, out1, out2, out3, out4, out5, out6, out7, out8, out9, out10, out11, out13, out15, out16, out17, out18, out19, out20, out21, out22, out23, out24, out25, out26, out27, out28, out29, out30, out31
  Register #(.width(32)) Status (
    .D(CP0RegIn), .en(demultiplexer_1_out12), .Q({Status_q[31:11], IM, Status_q[7:0]}), .clk(clk));  // open: clr
  Register #(.width(32)) Cause (.D(bit_extender_1_out), .en(HasInt), .Q(Cause_q), .clk(clk));  // open: clr
  Register #(.width(32)) EPC (.D(multiplexer_1_out), .en(or_1_out), .Q(OldPC), .clk(clk));  // open: clr
  not not_1 (IE, Status_q[0]);
  Multiplexer #(.select(5), .width(32), .enable("false")) multiplexer_2 (
    .in0({32{1'b0}}), .in1({32{1'b0}}), .in2({32{1'b0}}), .in3({32{1'b0}}), .in4({32{1'b0}}),
    .in5({32{1'b0}}), .in6({32{1'b0}}), .in7({32{1'b0}}), .in8({32{1'b0}}), .in9({32{1'b0}}),
    .in10({32{1'b0}}), .in11({32{1'b0}}), .in12({Status_q[31:11], IM, Status_q[7:0]}), .in13(Cause_q),
    .in14(OldPC), .in15({32{1'b0}}), .in16({32{1'b0}}), .in17({32{1'b0}}), .in18({32{1'b0}}),
    .in19({32{1'b0}}), .in20({32{1'b0}}), .in21({32{1'b0}}), .in22({32{1'b0}}), .in23({32{1'b0}}),
    .in24({32{1'b0}}), .in25({32{1'b0}}), .in26({32{1'b0}}), .in27({32{1'b0}}), .in28({32{1'b0}}),
    .in29({32{1'b0}}), .in30({32{1'b0}}), .in31({32{1'b0}}), .out(CP0RegOut), .sel(rd));
endmodule

module Counter (
  input  enable,
  input  clk,
  output [31:0] value
);

  wire [31:0] adder_1_out;

  Register #(.width(32)) register_1 (.D(adder_1_out), .en(enable), .Q(value), .clk(clk));  // open: clr
  Adder #(.width(32)) adder_1 (.a(32'h1), .b(value), .out(adder_1_out));  // open: cin, cout
endmodule

module Cnt1 (
  input  enable,
  input  clk,
  output value
);

  wire adder_1_out;

  Register #(.width(1)) register_1 (.D(adder_1_out), .en(enable), .Q(value), .clk(clk));  // open: clr
  Adder #(.width(1)) adder_1 (.a(1'b1), .b(value), .out(adder_1_out));  // open: cin, cout
endmodule
